// Logisim project imm_gen.circ as structural Verilog: 1 circuit, main circuit imm_gen
module imm_gen (
  input  [31:0] inst,
  input  [2:0] ImmSel,
  output [31:0] imm
);

  wire [31:0] B_Imm, I_Imm, J_Imm, S_Imm;

  assign I_Imm = {{20{inst[31]}}, inst[31:20]};  // Bit_Extender bit_extender_1
  assign S_Imm = {{20{inst[31]}}, {inst[31:25], inst[11:7]}};  // Bit_Extender bit_extender_2
  assign B_Imm = {{19{inst[31]}}, {inst[31], inst[7], inst[30:25], inst[11:8], 1'b0}};  // Bit_Extender bit_extender_3
  assign J_Imm = {{11{inst[31]}}, {inst[31], inst[19:12], inst[20], inst[30:21], 1'b0}};  // Bit_Extender bit_extender_4
  Multiplexer #(.enable("false"), .select(3), .width(32)) multiplexer_1 (
    .in0(I_Imm), .in1(S_Imm), .in2(B_Imm), .in3({inst[31:12], {12{1'b0}}}), .in4(J_Imm), .out(imm),
    .sel(ImmSel));  // open: in5, in6, in7

  // Other names for the same wires on the sheet: U_Imm[31:12] = inst[31:12]; Imm_Gen[31:0] = imm

  // Notes on the sheet:
  //   INPUTS to your circuit
  //   DON'T CHANGE THE LOCATIONS OF THE INPUTS AND OUTPUTS!
  //   OUTPUT from your circuit
endmodule
